# Fritzing sketch DoorBell (saved by Fritzing 0.9.3b)
circuit board: 8.46667cm x 5.64444cm
breadboards: 1

parts:
  U1 = ESP8266 WiFi Module [part_number=ESP8266]
  U2 = Optocoupler [package=THT]
  D1 = Diode [package=diode-1n4148]
  VCC1 = Battery
  R1 = Resistor [tolerance=±5% resistance=1k package=THT]
  J1 = Screw terminal - 2 pins [package=THT]

nets:
  N1: U1.VCC, U1.CH_PD, VCC1.+
  N2: U1.RST, U2.Pin_5
  N3: U1.GND, U2.Pin_4, VCC1.-
  N4: U2.Pin_1, D1.C, R1.Pin_1
  N5: U2.Pin_2, D1.A, J1.pin2
  N6: R1.Pin_0, J1.pin1

custom parts:
  ESP8266 WiFi Module: Generic WiFi Module based on the ESP8266 with onboard PCB antenna and UART communications
